// Logisim project Cache.circ as structural Verilog: 25 circuits, main circuit main
module main (
  input  EnableTestHalting,
  output [9:0] CorrectCounter,
  output [9:0] HitCounter,
  output [9:0] MissCounter,
  output [9:0] TestNumber,
  output [7:0] ByteRead,
  output [7:0] CorrectByteRead,
  output Halt
);

  wire and_3_out, and_4_out, and_5_out, CLK, CmdIsRead, Correct, CpuRead, CpuWrite, DidContain, HaltTesting,
       MaxItersReached, MemRead, MemWrite, not_1_out, not_2_out, not_4_out, NotDoneTesting, Ok2Count,
       or_1_out, Ready;
  wire [7:0] CpuWriteValue, MemAddress;
  wire [9:0] CpuAddress;
  wire [31:0] Line2Mem, LineFromMem;

  not not_1 (not_1_out, Ready);
  Clock clock_1 (.out(CLK));
  or or_1 (or_1_out, MaxItersReached, Ready);
  Counter #(.width(4), .max('h9)) MaxClocks (
    .load(Ready), .D(4'b0001), .count(not_1_out), .carry(MaxItersReached), .clk(CLK));  // open: Q, clr
  and and_1 (HaltTesting, EnableTestHalting, CmdIsRead, not_2_out);
  not not_2 (not_2_out, Correct);
  not not_3 (NotDoneTesting, Halt);
  Inputs inputs_1 (
    .HaltTesting(HaltTesting), .Ready(or_1_out), .CLK(CLK), .Done(Halt), .Read(CpuRead), .Write(CpuWrite),
    .Address(CpuAddress), .Value(CpuWriteValue), .TestNumber(TestNumber));
  Cache cache_1 (
    .CpuAddress(CpuAddress), .CpuRead(CpuRead), .CpuWrite(CpuWrite), .CpuWriteValue(CpuWriteValue),
    .CLK(CLK), .Ready(Ready), .DidContain(DidContain), .ByteRead(ByteRead), .MemAddress(MemAddress),
    .MemRead(MemRead), .MemWrite(MemWrite), .LineFromMem(LineFromMem), .Line2Mem(Line2Mem));
  // Probe on CpuRead
  // Probe on CpuWrite
  // Probe on CpuAddress
  // Probe on CpuWriteValue
  // Probe on TestNumber
  // Probe on CorrectByteRead
  // Probe on Correct
  // Probe on Ready
  // Probe on DidContain
  // Probe on ByteRead
  // Probe on MemAddress
  // Probe on MemRead
  // Probe on MemWrite
  // Probe on HitCounter
  // Probe on LineFromMem
  // Probe on Line2Mem
  not not_4 (not_4_out, HaltTesting);
  RAM #(.dataWidth(32), .bus("separate")) ram_1 (
    .addr(MemAddress), .din(Line2Mem), .data(LineFromMem), .str(MemWrite), .clk(CLK), .ld(MemRead));  // open: sel, clr
  and and_2 (Ok2Count, Ready, not_4_out, NotDoneTesting);
  and and_3 (and_3_out, Correct, Ok2Count);
  and and_4 (and_4_out, DidContain, Ok2Count);
  and and_5 (and_5_out, MemRead, NotDoneTesting);
  Checker checker_1 (
    .TestNumber(TestNumber), .YourByteRead(ByteRead), .CmdIsRead(CmdIsRead),
    .CorrectByteRead(CorrectByteRead), .Correct(Correct));
  Counter #(.width(10), .max('h3ff)) u_CorrectCounter (
    .count(and_3_out), .Q(CorrectCounter), .clk(CLK));  // open: load, D, carry, clr
  Counter #(.width(10), .max('h3ff)) u_HitCounter (
    .count(and_4_out), .Q(HitCounter), .clk(CLK));  // open: load, D, carry, clr
  Counter #(.width(10), .max('h3ff)) u_MissCounter (
    .count(and_5_out), .Q(MissCounter), .clk(CLK));  // open: load, D, carry, clr
  // Probe on CorrectCounter
  // Probe on HitCounter
  // Probe on MissCounter

  // Other names for the same wires on the sheet: DoneTesting = Halt

  // Notes on the sheet:
  //   Your Answer Inside Here
  //   There seem to be a lot of cases where ByteRead == CorrectByteRead & CpuRead, but CmdIsRead is false
  //   Therefore, my correct counter does not go up.
  //   I went through the test manually (which took too much time) and kept track of all cases where ByteRead == CorrectByteRead & Ready & CpuRead
  //   I believe I was correct in test cases 9, 16, 25, 26, 35, 40, 47, 50, 59, 68, 80, 83, 102, 109, 117 
  //   Therefore, I believe my actual correct counter should be 16 instead of 1
endmodule

module Cache (
  input  [9:0] CpuAddress,
  input  CpuRead,
  input  CpuWrite,
  input  [7:0] CpuWriteValue,
  input  CLK,
  input  [31:0] LineFromMem,
  output Ready,
  output DidContain,
  output [7:0] ByteRead,
  output [7:0] MemAddress,
  output MemRead,
  output MemWrite,
  output [31:0] Line2Mem
);

  wire ctrl_cachedidcontain_1_didcontaincontrol, demultiplexer_1_out0, demultiplexer_1_out1,
       demultiplexer_2_out0, demultiplexer_2_out1, Dirty, Hit, multiplexer_1_out, multiplexer_2_out,
       multiplexer_4_out, multiplexer_5_out, multiplexer_6_out, multiplexer_8_out, multiplexer_9_out,
       S_0_Dirty, S_0_Hit, S_0_Read, S_0_Valid, S_0_Write, S_1_Dirty, S_1_Hit, S_1_Read, S_1_Valid,
       S_1_Write, S_CpuRead, S_CpuWrite, StateCacheRead, StateCacheWrite, Valid, Valid_Inputs;
  wire [1:0] Offset;
  wire [2:0] ctrl_cachenextstate_1_s_02, State;
  wire [7:0] multiplexer_10_out, multiplexer_16_out, multiplexer_17_out, multiplexer_18_out,
       multiplexer_19_out, S_CpuWriteValue;
  wire [9:0] multiplexer_7_out, multiplexer_14_out, multiplexer_15_out, S_CpuAddress;
  wire [31:0] multiplexer_11_out, S_0_Line2Mem, S_0DataOut, S_1_Line2Mem, S_1DataOut;

  Multiplexer #(.enable("false")) multiplexer_1 (
    .in0(S_CpuWrite), .in1(CpuWrite), .out(multiplexer_1_out), .sel(Valid_Inputs));
  Demultiplexer #(.disabled(0), .enable("false")) demultiplexer_1 (
    .out0(demultiplexer_1_out0), .out1(demultiplexer_1_out1), .in(multiplexer_1_out), .sel(MemAddress[0]));
  Demultiplexer #(.disabled(0), .enable("false")) demultiplexer_2 (
    .out0(demultiplexer_2_out0), .out1(demultiplexer_2_out1), .in(multiplexer_2_out), .sel(MemAddress[0]));
  Multiplexer #(.enable("false")) multiplexer_2 (
    .in0(S_CpuRead), .in1(CpuRead), .out(multiplexer_2_out), .sel(Valid_Inputs));
  and and_1 (S_0_Read, StateCacheRead, demultiplexer_2_out0);
  and and_2 (S_1_Read, demultiplexer_2_out1, StateCacheRead);
  CTRL_CacheStateCacheWrite ctrl_cachestatecachewrite_1 (.State(State), .Write(StateCacheWrite));
  CTRL_CacheStateCacheRead ctrl_cachestatecacheread_1 (.State(State), .Read(StateCacheRead));
  // Probe on MemAddress[7:1]
  // Probe on MemAddress[0]
  // Probe on Offset
  // Probe on S_CpuAddress
  // Probe on S_CpuRead
  // Probe on S_CpuWrite
  // Probe on S_CpuWriteValue
  // Probe on State
  and and_3 (S_0_Write, StateCacheWrite, demultiplexer_1_out0);
  and and_4 (S_1_Write, demultiplexer_1_out1, StateCacheWrite);
  CTRL_CacheValidInput ctrl_cachevalidinput_1 (.State(State), .ValidInputs(Valid_Inputs));
  CTRL_CacheReady ctrl_cacheready_1 (.State(State), .Ready(Ready));
  CTRL_CacheMemRead ctrl_cachememread_1 (.State(State), .MemRead(MemRead));
  CTRL_CacheMemWrite ctrl_cachememwrite_1 (.State(State), .MemWrite(MemWrite));
  Multiplexer #(.width(10), .enable("false")) multiplexer_3 (
    .in0(S_CpuAddress), .in1(CpuAddress), .out({MemAddress, Offset}), .sel(Valid_Inputs));
  Multiplexer #(.enable("false")) multiplexer_4 (
    .in0(S_CpuRead), .in1(CpuRead), .out(multiplexer_4_out), .sel(Valid_Inputs));
  Multiplexer #(.enable("false")) multiplexer_5 (
    .in0(S_CpuWrite), .in1(CpuWrite), .out(multiplexer_5_out), .sel(Valid_Inputs));
  CTRL_CacheDidContain ctrl_cachedidcontain_1 (
    .S2(State[2]), .S1(State[1]), .S12(State[0]), .DidContainControl(ctrl_cachedidcontain_1_didcontaincontrol));
  Multiplexer #(.enable("false")) multiplexer_6 (
    .in0(DidContain), .in1(Hit), .out(multiplexer_6_out), .sel(ctrl_cachedidcontain_1_didcontaincontrol));
  CTRL_CacheNextState ctrl_cachenextstate_1 (
    .S_2(State[2]), .S_1(State[1]), .S_0(State[0]), .Write(multiplexer_5_out), .Read(multiplexer_4_out),
    .Hit(Hit), .Dirty(Dirty), .Valid(Valid), .S_22(ctrl_cachenextstate_1_s_02[2]),
    .S_12(ctrl_cachenextstate_1_s_02[1]), .S_02(ctrl_cachenextstate_1_s_02[0]));
  Register #(.width(1)) u_DidContain (.D(multiplexer_6_out), .Q(DidContain), .clk(CLK));  // open: en, clr
  Register #(.width(10)) u_CpuAddress (.D(multiplexer_7_out), .Q(S_CpuAddress), .clk(CLK));  // open: en, clr
  Multiplexer #(.width(10), .enable("false")) multiplexer_7 (
    .in0(S_CpuAddress), .in1(CpuAddress), .out(multiplexer_7_out), .sel(Valid_Inputs));
  Register #(.width(1)) u_CpuRead (.D(multiplexer_8_out), .Q(S_CpuRead), .clk(CLK));  // open: en, clr
  Multiplexer #(.enable("false")) multiplexer_8 (
    .in0(S_CpuRead), .in1(CpuRead), .out(multiplexer_8_out), .sel(Valid_Inputs));
  Multiplexer #(.enable("false")) multiplexer_9 (
    .in0(S_CpuWrite), .in1(CpuWrite), .out(multiplexer_9_out), .sel(Valid_Inputs));
  Register #(.width(1)) u_CpuWrite (.D(multiplexer_9_out), .Q(S_CpuWrite), .clk(CLK));  // open: en, clr
  Multiplexer #(.width(8), .enable("false")) multiplexer_10 (
    .in0(S_CpuWriteValue), .in1(CpuWriteValue), .out(multiplexer_10_out), .sel(Valid_Inputs));
  Register u_S_CpuWriteValue (.D(multiplexer_10_out), .Q(S_CpuWriteValue), .clk(CLK));  // open: en, clr
  Register #(.width(3)) u_State (.D(ctrl_cachenextstate_1_s_02), .Q(State), .clk(CLK));  // open: en, clr
  Multiplexer #(.width(32), .enable("false")) multiplexer_11 (
    .in0(S_0DataOut), .in1(S_1DataOut), .out(multiplexer_11_out), .sel(MemAddress[0]));
  Multiplexer #(.enable("false")) multiplexer_12 (.in0(S_0_Dirty), .in1(S_1_Dirty), .out(Dirty), .sel(MemAddress[0]));
  Multiplexer #(.enable("false")) multiplexer_13 (.in0(S_0_Hit), .in1(S_1_Hit), .out(Hit), .sel(MemAddress[0]));
  Multiplexer #(.width(10), .enable("false")) multiplexer_14 (
    .in0(S_CpuAddress), .in1(CpuAddress), .out(multiplexer_14_out), .sel(Valid_Inputs));
  Multiplexer #(.width(10), .enable("false")) multiplexer_15 (
    .in0(S_CpuAddress), .in1(CpuAddress), .out(multiplexer_15_out), .sel(Valid_Inputs));
  Multiplexer #(.select(2), .width(8), .enable("false")) multiplexer_16 (
    .in0(multiplexer_11_out[7:0]), .in1(multiplexer_11_out[15:8]), .in2(multiplexer_11_out[23:16]),
    .in3(multiplexer_11_out[31:24]), .out(multiplexer_16_out), .sel(Offset));
  Multiplexer #(.width(8), .enable("false")) multiplexer_17 (
    .in0(S_CpuWriteValue), .in1(CpuWriteValue), .out(multiplexer_17_out), .sel(Valid_Inputs));
  Multiplexer #(.width(8), .enable("false")) multiplexer_18 (
    .in0(S_CpuWriteValue), .in1(CpuWriteValue), .out(multiplexer_18_out), .sel(Valid_Inputs));
  Multiplexer #(.width(8), .enable("false")) multiplexer_19 (
    .in0(ByteRead), .in1(multiplexer_16_out), .out(multiplexer_19_out), .sel(Hit));
  Register State_2 (.D(multiplexer_19_out), .Q(ByteRead), .clk(CLK));  // open: en, clr
  Multiplexer #(.enable("false")) multiplexer_20 (.in0(S_0_Valid), .in1(S_1_Valid), .out(Valid), .sel(MemAddress[0]));
  Multiplexer #(.width(32), .enable("false")) multiplexer_21 (
    .in0(S_0_Line2Mem), .in1(S_1_Line2Mem), .out(Line2Mem), .sel(MemAddress[0]));
  Set Set_0 (
    .CLK(CLK), .MemAddr(multiplexer_14_out), .DataIn(LineFromMem), .WriteVal(multiplexer_17_out),
    .Write(S_0_Write), .Read(S_0_Read), .State(State), .Hit(S_0_Hit), .Dirty(S_0_Dirty), .Valid(S_0_Valid),
    .DataOut(S_0DataOut), .Line2Mem(S_0_Line2Mem));
  Set Set_1 (
    .CLK(CLK), .MemAddr(multiplexer_15_out), .DataIn(LineFromMem), .WriteVal(multiplexer_18_out),
    .Write(S_1_Write), .Read(S_1_Read), .State(State), .Hit(S_1_Hit), .Dirty(S_1_Dirty), .Valid(S_1_Valid),
    .DataOut(S_1DataOut), .Line2Mem(S_1_Line2Mem));

  // Other names for the same wires on the sheet: Set = MemAddress[0]; Tag[6:0] = MemAddress[7:1]

  // Notes on the sheet:
  //   Address Bits = 10
  //   Line Size = 4
  //   W = 3
  //   Given Inputs
  //   Num Sets = 2
  //   C =4*3*2 = 24bytes
  //   Pins
  //   Tag bits = 7
  //   Control Values
  //   Stored Values
  //   A Number of my byte read values are correct, but I cannot get them to display when 
  //   Ready = 1 without screwing them up :(
  //   In trying to fix it, I ended up making it much much worse, and I can't find my way back
  //   I had about 50% success earlier...
endmodule

module Inputs (
  input  HaltTesting,
  input  Ready,
  input  CLK,
  output Done,
  output Read,
  output Write,
  output [9:0] Address,
  output [7:0] Value,
  output [9:0] TestNumber
);

  wire and_1_out, not_1_out, not_2_out;

  not not_1 (not_1_out, HaltTesting);
  not not_2 (not_2_out, Done);
  Counter #(.width(10), .max('h3ff), .ongoal("stay")) u_TestNumber (
    .count(and_1_out), .Q(TestNumber), .clk(CLK));  // open: load, D, carry, clr
  and and_1 (and_1_out, not_1_out, Ready, not_2_out);
  ROM #(.addrWidth(10), .dataWidth(21)) rom_1 (
    .addr(TestNumber), .data({Done, Read, Write, Address, Value}));  // open: sel

  // Notes on the sheet:
  //   contents of rom_1 (hex, n*v repeats v):
  //   80882 83fe6 4306b 83e0e 43701 42275 8280f 80304 41bd8 84371 43f77 41d70 4250b 44733 8253d 440d8
  //   82691 440c9 83d7c 43558 446bf 83837 842c9 43e0f 4059d 41556 80166 833b0 43a89 83142 8361c 42e66
  //   43eb6 42c00 43a0e 8165c 84682 8092a 83907 41f89 817b0 40855 82056 425e8 43ff2 8039f 42bd7 82137
  //   4416b 40273 8324a 814e4 44570 41c0f 429da 82640 8069c 8099e 414d5 41004 81beb 84113 419b1 81add
  //   83f35 425ff 829cd 40250 82945 4366d 40cc2 444f8 80814 81156 8446d 42a82 42bae 82578 41135 405d0
  //   8304b 82b3a 40972 822ba 4443a 42337 82506 80bd3 80560 83552 83955 81434 43096 43da1 81aa2 80305
  //   428e6 428cc 808a2 40e80 845f0 4215d 82765 82e29 40be5 82b74 42715 417a2 41fab 8452f 81c0a 83325
  //   44624 80205 42dfc 41333 40958 81348 42736 41069 84510 44669 826dd 8067e 408e4 44680 444e8 832ad
  //   821f8 83509 82d46 81184 432cd 80b77 4005a 440e0 81ea0 43d73 42b8c 80624 41468 42699 415ed 80fc1 0
  //   100000
endmodule

module Checker (
  input  [9:0] TestNumber,
  input  [7:0] YourByteRead,
  output CmdIsRead,
  output [7:0] CorrectByteRead,
  output Correct
);

  wire comparator_1_eq;
  wire [9:0] subtractor_1_out;

  // Probe on TestNumber
  Subtractor #(.width(10)) subtractor_1 (.a(TestNumber), .b(10'h1), .out(subtractor_1_out));  // open: bin, bout
  ROM #(.addrWidth(10), .dataWidth(9)) rom_1 (
    .addr(subtractor_1_out), .data({CmdIsRead, CorrectByteRead}));  // open: sel
  Comparator #(.mode("unsigned")) comparator_1 (
    .a(YourByteRead), .b(CorrectByteRead), .eq(comparator_1_eq));  // open: gt, lt
  and and_1 (Correct, comparator_1_eq, CmdIsRead);

  // Other names for the same wires on the sheet: Test_Number[9:0] = TestNumber

  // Notes on the sheet:
  //   Read Solutions
  //   contents of rom_1 (hex, n*v repeats v):
  //   1a3 1dc 6b 125 1 75 1dc 1c3 d8 1ab 77 70 b 33 10b d8 1c3 c9 174 58 bf 153 199 f 9d 56 1bb 13b 89 16c
  //   180 66 b6 0 e 107 1bf 1d8 167 89 118 55 1a2 e8 f2 1c3 d7 142 6b 73 1ab 18c 70 f da 1c3 14c 1d8 d5 4
  //   1d8 16b b1 1f4 1f2 ff 1da 50 1da 6d c2 f8 155 1c6 1f8 82 ae 1ff 35 d0 16b 1ae 72 175 3a 37 1ff 173
  //   1d0 158 167 1d5 96 a1 1f4 1c3 e6 cc 155 80 170 5d 1e6 166 e5 1ae 15 a2 ab 170 10f 13b 24 150 fc 33
  //   58 133 36 69 170 69 1c3 14c e4 80 e8 1ab 15d 158 1fc 135 cd 1e5 5a e0 104 73 8c 14c 68 99 ed 1a6
endmodule

module Set (
  input  CLK,
  input  [9:0] MemAddr,
  input  [31:0] DataIn,
  input  [7:0] WriteVal,
  input  Write,
  input  Read,
  input  [2:0] State,
  output Hit,
  output Dirty,
  output Valid,
  output [31:0] DataOut,
  output [31:0] Line2Mem
);

  wire and_1_out, and_2_out, and_3_out, and_11_out, and_12_out, and_13_out, and_14_out, and_15_out,
       and_16_out, and_17_out, and_18_out, and_19_out, and_20_out, and_21_out, and_22_out, and_23_out,
       and_24_out, and_25_out, Block0Dirty, Block0Read, Block0Valid, Block0Write, Block1Dirty, Block1Read,
       Block1Valid, Block1Write, Block2Dirty, Block2Read, Block2Valid, Block2Write, comparator_1_eq,
       comparator_2_eq, comparator_3_eq, comparator_4_eq, comparator_5_eq, comparator_6_eq, comparator_7_eq,
       comparator_8_eq, comparator_9_eq, comparator_10_eq, comparator_11_eq, comparator_12_eq,
       comparator_13_eq, comparator_14_eq, comparator_15_eq, comparator_16_eq, comparator_17_eq,
       comparator_18_eq, comparator_19_eq, comparator_20_eq, comparator_21_eq, comparator_22_eq,
       comparator_23_eq, comparator_24_eq, ReadState;
  wire [1:0] AgeAccessed, Block0Age, Block0AgeControl, Block1Age, Block1AgeControl, Block2Age,
       Block2AgeControl, ctrl_setageacessed_1_s0, DataOutControl, Line2MemControl;
  wire [6:0] Block0Tag, Block1Tag, Block2Tag;
  wire [31:0] Block0DataOut, Block1DataOut, Block2DataOut;

  Comparator #(.width(7), .mode("unsigned")) comparator_1 (
    .a(Block2Tag), .b(MemAddr[9:3]), .eq(comparator_1_eq));  // open: gt, lt
  Comparator #(.width(7), .mode("unsigned")) comparator_2 (
    .a(Block1Tag), .b(MemAddr[9:3]), .eq(comparator_2_eq));  // open: gt, lt
  and and_1 (and_1_out, comparator_1_eq, Block2Valid);
  Comparator #(.width(7), .mode("unsigned")) comparator_3 (
    .a(Block0Tag), .b(MemAddr[9:3]), .eq(comparator_3_eq));  // open: gt, lt
  and and_2 (and_2_out, comparator_2_eq, Block1Valid);
  CTRL_SetNewAgeMux ctrl_setnewagemux_1 (
    .State(State), .Age(Block0Age), .AgeAccessed(AgeAccessed), .AgeControl(Block0AgeControl));
  CTRL_SetNewAgeMux ctrl_setnewagemux_2 (
    .State(State), .Age(Block1Age), .AgeAccessed(AgeAccessed), .AgeControl(Block1AgeControl));
  CTRL_SetNewAgeMux ctrl_setnewagemux_3 (
    .State(State), .Age(Block2Age), .AgeAccessed(AgeAccessed), .AgeControl(Block2AgeControl));
  and and_3 (and_3_out, comparator_3_eq, Block0Valid);
  CTRL_SetAgeAcessed ctrl_setageacessed_1 (
    .B0(and_3_out), .B1(and_2_out), .B12(and_1_out), .S1(ctrl_setageacessed_1_s0[1]),
    .S0(ctrl_setageacessed_1_s0[0]));
  Multiplexer #(.select(2), .width(2), .enable("false")) multiplexer_1 (
    .in0(Block0Age), .in1(Block1Age), .in2(Block2Age), .out(AgeAccessed), .sel(ctrl_setageacessed_1_s0));  // open: in3
  and and_4 (ReadState, State[2], State[1], State[0]);
  Comparator #(.width(2), .mode("unsigned")) comparator_4 (
    .a(Block0Age), .b(2'b10), .eq(comparator_4_eq));  // open: gt, lt
  Comparator #(.width(2), .mode("unsigned")) comparator_5 (
    .a(Block1Age), .b(2'b10), .eq(comparator_5_eq));  // open: gt, lt
  Comparator #(.width(2), .mode("unsigned")) comparator_6 (
    .a(Block2Age), .b(2'b10), .eq(comparator_6_eq));  // open: gt, lt
  Comparator #(.width(7), .mode("unsigned")) comparator_7 (
    .a(Block0Tag), .b(MemAddr[9:3]), .eq(comparator_7_eq));  // open: gt, lt
  Comparator #(.width(7), .mode("unsigned")) comparator_8 (
    .a(Block1Tag), .b(MemAddr[9:3]), .eq(comparator_8_eq));  // open: gt, lt
  Comparator #(.width(7), .mode("unsigned")) comparator_9 (
    .a(Block2Tag), .b(MemAddr[9:3]), .eq(comparator_9_eq));  // open: gt, lt
  and and_5 (Block0Read, comparator_4_eq, ReadState);
  and and_6 (Block1Read, comparator_5_eq, ReadState);
  and and_7 (Block2Read, comparator_6_eq, ReadState);
  and and_8 (Block0Write, comparator_7_eq, Block0Valid, Write);
  and and_9 (Block1Write, comparator_8_eq, Block1Valid, Write);
  and and_10 (Block2Write, comparator_9_eq, Block2Valid, Write);
  Comparator #(.width(2), .mode("unsigned")) comparator_10 (
    .a(Block0Age), .b(2'b10), .eq(comparator_10_eq));  // open: gt, lt
  Comparator #(.width(2), .mode("unsigned")) comparator_11 (
    .a(Block1Age), .b(2'b10), .eq(comparator_11_eq));  // open: gt, lt
  Comparator #(.width(2), .mode("unsigned")) comparator_12 (
    .a(Block2Age), .b(2'b10), .eq(comparator_12_eq));  // open: gt, lt
  and and_11 (and_11_out, comparator_10_eq, Block0Dirty);
  and and_12 (and_12_out, comparator_11_eq, Block1Dirty);
  and and_13 (and_13_out, comparator_12_eq, Block2Dirty);
  Multiplexer #(.select(2), .width(32), .enable("false")) multiplexer_2 (
    .in0(Block0DataOut), .in1(Block1DataOut), .in2(Block2DataOut), .out(Line2Mem), .sel(Line2MemControl));  // open: in3
  CTRL_SetLine2Mem ctrl_setline2mem_1 (
    .B0Dirty(and_11_out), .B1Dirty(and_12_out), .B2Dirty(and_13_out), .C1(Line2MemControl[1]),
    .C0(Line2MemControl[0]));
  Block Block_1 (
    .CLK(CLK), .DataIn(DataIn), .WriteVal(WriteVal), .AgeInit(2'b01), .AgeControl(Block1AgeControl),
    .Read(Block1Read), .Write(Block1Write), .Offset(MemAddr[1:0]), .In_Tag(MemAddr[9:3]),
    .DataOut(Block1DataOut), .Age(Block1Age), .Tag(Block1Tag), .Valid(Block1Valid), .Dirty(Block1Dirty));
  Block Block_2 (
    .CLK(CLK), .DataIn(DataIn), .WriteVal(WriteVal), .AgeInit(2'b00), .AgeControl(Block2AgeControl),
    .Read(Block2Read), .Write(Block2Write), .Offset(MemAddr[1:0]), .In_Tag(MemAddr[9:3]),
    .DataOut(Block2DataOut), .Age(Block2Age), .Tag(Block2Tag), .Valid(Block2Valid), .Dirty(Block2Dirty));
  Block Block_0 (
    .CLK(CLK), .DataIn(DataIn), .WriteVal(WriteVal), .AgeInit(2'b10), .AgeControl(Block0AgeControl),
    .Read(Block0Read), .Write(Block0Write), .Offset(MemAddr[1:0]), .In_Tag(MemAddr[9:3]),
    .DataOut(Block0DataOut), .Age(Block0Age), .Tag(Block0Tag), .Valid(Block0Valid), .Dirty(Block0Dirty));
  Comparator #(.width(2), .mode("unsigned")) comparator_13 (
    .a(Block2Age), .b(2'b10), .eq(comparator_13_eq));  // open: gt, lt
  Comparator #(.width(7), .mode("unsigned")) comparator_14 (
    .a(Block0Tag), .b(MemAddr[9:3]), .eq(comparator_14_eq));  // open: gt, lt
  Comparator #(.width(7), .mode("unsigned")) comparator_15 (
    .a(Block1Tag), .b(MemAddr[9:3]), .eq(comparator_15_eq));  // open: gt, lt
  Comparator #(.width(7), .mode("unsigned")) comparator_16 (
    .a(Block2Tag), .b(MemAddr[9:3]), .eq(comparator_16_eq));  // open: gt, lt
  Comparator #(.width(2), .mode("unsigned")) comparator_17 (
    .a(Block0Age), .b(2'b10), .eq(comparator_17_eq));  // open: gt, lt
  Comparator #(.width(2), .mode("unsigned")) comparator_18 (
    .a(Block1Age), .b(2'b10), .eq(comparator_18_eq));  // open: gt, lt
  Comparator #(.width(2), .mode("unsigned")) comparator_19 (
    .a(Block2Age), .b(2'b10), .eq(comparator_19_eq));  // open: gt, lt
  Comparator #(.width(7), .mode("unsigned")) comparator_20 (
    .a(Block0Tag), .b(MemAddr[9:3]), .eq(comparator_20_eq));  // open: gt, lt
  Comparator #(.width(7), .mode("unsigned")) comparator_21 (
    .a(Block1Tag), .b(MemAddr[9:3]), .eq(comparator_21_eq));  // open: gt, lt
  Comparator #(.width(7), .mode("unsigned")) comparator_22 (
    .a(Block2Tag), .b(MemAddr[9:3]), .eq(comparator_22_eq));  // open: gt, lt
  Comparator #(.width(2), .mode("unsigned")) comparator_23 (
    .a(Block0Age), .b(2'b10), .eq(comparator_23_eq));  // open: gt, lt
  Comparator #(.width(2), .mode("unsigned")) comparator_24 (
    .a(Block1Age), .b(2'b10), .eq(comparator_24_eq));  // open: gt, lt
  and and_14 (and_14_out, comparator_13_eq, Block2Dirty);
  Multiplexer #(.select(2), .width(32), .enable("false")) multiplexer_3 (
    .in0(Block0DataOut), .in1(Block1DataOut), .in2(Block2DataOut), .out(DataOut), .sel(DataOutControl));  // open: in3
  and and_15 (and_15_out, comparator_14_eq, Block0Valid);
  and and_16 (and_16_out, comparator_15_eq, Block1Valid);
  and and_17 (and_17_out, comparator_16_eq, Block2Valid);
  and and_18 (and_18_out, comparator_17_eq, Block0Dirty);
  and and_19 (and_19_out, comparator_18_eq, Block1Dirty);
  and and_20 (and_20_out, comparator_19_eq, Block2Dirty);
  and and_21 (and_21_out, comparator_20_eq, Block0Valid);
  and and_22 (and_22_out, comparator_21_eq, Block1Valid);
  and and_23 (and_23_out, comparator_22_eq, Block2Valid);
  and and_24 (and_24_out, comparator_23_eq, Block0Dirty);
  and and_25 (and_25_out, comparator_24_eq, Block1Dirty);
  or or_1 (Dirty, and_24_out, and_25_out, and_14_out);
  or or_2 (Hit, and_21_out, and_22_out, and_23_out);
  CTRL_SetDataOut ctrl_setdataout_1 (
    .B0Hit(and_15_out), .B1Hit(and_16_out), .B2Hit(and_17_out), .B0Dirty(and_18_out), .B1Dirty(and_19_out),
    .B2Dirty(and_20_out), .C1(DataOutControl[1]), .C0(DataOutControl[0]));

  assign Valid = 1'b1;

  // Other names for the same wires on the sheet: Offset[1:0] = MemAddr[1:0]; Set = MemAddr[2];
  //   Tag[6:0] = MemAddr[9:3]

  // Notes on the sheet:
  //   Not perfect Set, but pretty good
  //   About 99% evicts correct block and finds hit and dirty before single tick
  //   I had a lot of trouble getting the age to work, and created a number of subcircuits to control that
  //   This circuit is a little harder to follow, as I made a lot of mistakes in designing it and had to shove things in
  //   Only issue I could not figure out at all is why the DataOut is often incorrect
  //   It used to have higher success rate (around 50%) but, in trying to fix it, I royally messed it up
  //   Still has almost 100% hit and miss accuracy to correct number, however.
  //   Therefore, the values are stored in the cache. I just can't display them accurately for some reason
  //   Obviously the reason is my logic, but I couldn't figure out where I went wrong.
  //   If I had a little more time to redesign again from scratch, I think I could make it a lot better.
  //   I think a lot of the struggle of the project was just understanding what to do.
  //   But, given it is a final project, I couldn't dedicate as much time to it as necessary to a newcomer to circuits
endmodule

module Block (
  input  CLK,
  input  [31:0] DataIn,
  input  [7:0] WriteVal,
  input  [1:0] AgeInit,
  input  [1:0] AgeControl,
  input  Read,
  input  Write,
  input  [1:0] Offset,
  input  [6:0] In_Tag,
  output [31:0] DataOut,
  output [1:0] Age,
  output [6:0] Tag,
  output Valid,
  output Dirty
);

  wire multiplexer_6_out, multiplexer_7_out;
  wire [1:0] adder_1_out, Byte_0_Ctrl, Byte_1_Ctrl, Byte_2_Ctrl, Byte_3_Ctrl, Dirty_Control,
       multiplexer_5_out;
  wire [6:0] multiplexer_8_out;
  wire [7:0] multiplexer_1_out, multiplexer_2_out, multiplexer_3_out, multiplexer_4_out;

  CTRL_BlockByte0Ctrl ctrl_blockbyte0ctrl_1 (
    .Read(Read), .Write(Write), .O1(Offset[1]), .O0(Offset[0]), .C1(Byte_0_Ctrl[1]), .C0(Byte_0_Ctrl[0]));
  CTRL_BlockByte1Ctrl ctrl_blockbyte1ctrl_1 (
    .Read(Read), .Write(Write), .O1(Offset[1]), .O0(Offset[0]), .C1(Byte_1_Ctrl[1]), .C0(Byte_1_Ctrl[0]));
  CTRL_BlockByte2Ctrl ctrl_blockbyte2ctrl_1 (
    .Read(Read), .Write(Write), .O1(Offset[1]), .O0(Offset[0]), .C1(Byte_2_Ctrl[1]), .C0(Byte_2_Ctrl[0]));
  CTRL_BlockByte3Ctrl ctrl_blockbyte3ctrl_1 (
    .Read(Read), .Write(Write), .O1(Offset[1]), .O0(Offset[0]), .C1(Byte_3_Ctrl[1]), .C0(Byte_3_Ctrl[0]));
  CTRL_BlockDirtyControl ctrl_blockdirtycontrol_1 (
    .Write(Write), .Read(Read), .C2(Dirty_Control[1]), .C1(Dirty_Control[0]));
  Multiplexer #(.select(2), .width(8), .enable("false")) multiplexer_1 (
    .in0(DataOut[7:0]), .in1(DataIn[7:0]), .in2(WriteVal), .out(multiplexer_1_out), .sel(Byte_0_Ctrl));  // open: in3
  Multiplexer #(.select(2), .width(8), .enable("false")) multiplexer_2 (
    .in0(DataOut[15:8]), .in1(DataIn[15:8]), .in2(WriteVal), .out(multiplexer_2_out), .sel(Byte_1_Ctrl));  // open: in3
  Multiplexer #(.select(2), .width(8), .enable("false")) multiplexer_3 (
    .in0(DataOut[23:16]), .in1(DataIn[23:16]), .in2(WriteVal), .out(multiplexer_3_out), .sel(Byte_2_Ctrl));  // open: in3
  Multiplexer #(.select(2), .width(8), .enable("false")) multiplexer_4 (
    .in0(DataOut[31:24]), .in1(DataIn[31:24]), .in2(WriteVal), .out(multiplexer_4_out), .sel(Byte_3_Ctrl));  // open: in3
  Register Byte_3 (.D(multiplexer_4_out), .Q(DataOut[31:24]), .clk(CLK));  // open: en, clr
  Register Byte_0 (.D(multiplexer_1_out), .Q(DataOut[7:0]), .clk(CLK));  // open: en, clr
  Register Byte_1 (.D(multiplexer_2_out), .Q(DataOut[15:8]), .clk(CLK));  // open: en, clr
  Register Byte_2 (.D(multiplexer_3_out), .Q(DataOut[23:16]), .clk(CLK));  // open: en, clr
  Adder #(.width(2)) adder_1 (.a(Age), .b(2'b01), .out(adder_1_out));  // open: cin, cout
  Register #(.width(2)) u_Age (.D(multiplexer_5_out), .Q(Age), .clk(CLK));  // open: en, clr
  Multiplexer #(.select(2), .width(2), .enable("false")) multiplexer_5 (
    .in0(AgeInit), .in1(2'b00), .in2(Age), .in3(adder_1_out), .out(multiplexer_5_out), .sel(AgeControl));
  Multiplexer #(.enable("false")) multiplexer_6 (.in0(Valid), .in1(1'b1), .out(multiplexer_6_out), .sel(Read));
  Register #(.width(1)) u_Valid (.D(multiplexer_6_out), .Q(Valid), .clk(CLK));  // open: en, clr
  Register #(.width(1)) u_Dirty (.D(multiplexer_7_out), .Q(Dirty), .clk(CLK));  // open: en, clr
  Multiplexer #(.select(2), .enable("false")) multiplexer_7 (
    .in0(Dirty), .in1(1'b0), .in2(1'b1), .out(multiplexer_7_out), .sel(Dirty_Control));  // open: in3
  Multiplexer #(.width(7), .enable("false")) multiplexer_8 (
    .in0(Tag), .in1(In_Tag), .out(multiplexer_8_out), .sel(Read));
  Register #(.width(7)) u_Tag (.D(multiplexer_8_out), .Q(Tag), .clk(CLK));  // open: en, clr

  // Other names for the same wires on the sheet: In_Byte_0[7:0] = DataIn[7:0]; In_Byte_1[7:0] = DataIn[15:8];
  //   In_Byte_2[7:0] = DataIn[23:16]; In_Byte_3[7:0] = DataIn[31:24]; Byte_0[7:0] = DataOut[7:0];
  //   Byte_1[7:0] = DataOut[15:8]; Byte_2[7:0] = DataOut[23:16]; Byte_3[7:0] = DataOut[31:24]

  // Notes on the sheet:
  //   Fully Functioning Block
  //   Also, quite well organized
  //   Separate registers for every byte
  //   As well as separate control subcircuits
endmodule

module CTRL_CacheNextState (
  input  S_2,
  input  S_1,
  input  S_0,
  input  Write,
  input  Read,
  input  Hit,
  input  Dirty,
  input  Valid,
  output S_22,
  output S_12,
  output S_02
);

  wire and_1_out, and_2_out, and_3_out, and_4_out, and_5_out, and_6_out, and_7_out, and_8_out, and_9_out,
       and_10_out, and_11_out, and_12_out, and_13_out, and_14_out, and_15_out, and_16_out, not_1_out,
       not_2_out, not_3_out, not_4_out, not_5_out, not_6_out, not_7_out, not_8_out, not_9_out, not_10_out,
       not_11_out, not_12_out, not_13_out, not_14_out, not_15_out, not_16_out, not_17_out, not_18_out,
       not_19_out, not_20_out, not_21_out;

  and and_1 (and_1_out, S_1, Read, not_1_out);
  not not_1 (not_1_out, Dirty);
  and and_2 (and_2_out, S_1, Read, Hit, Valid);
  and and_3 (and_3_out, S_1, Write, not_2_out);
  not not_2 (not_2_out, Dirty);
  and and_4 (and_4_out, S_1, Write, Hit, Valid);
  and and_5 (and_5_out, S_2, S_1);
  not not_3 (not_3_out, S_2);
  and and_6 (and_6_out, not_3_out, not_4_out);
  not not_4 (not_4_out, Read);
  not not_5 (not_5_out, S_2);
  and and_7 (and_7_out, not_5_out, not_6_out);
  not not_6 (not_6_out, Hit);
  not not_7 (not_7_out, S_2);
  and and_8 (and_8_out, not_7_out, not_8_out);
  not not_8 (not_8_out, Valid);
  not not_9 (not_9_out, S_1);
  and and_9 (and_9_out, not_9_out, not_10_out);
  not not_10 (not_10_out, S_0);
  not not_11 (not_11_out, S_2);
  and and_10 (and_10_out, not_11_out, S_0);
  not not_12 (not_12_out, S_2);
  not not_13 (not_13_out, S_2);
  not not_14 (not_14_out, Hit);
  not not_15 (not_15_out, S_2);
  not not_16 (not_16_out, Valid);
  not not_17 (not_17_out, S_2);
  not not_18 (not_18_out, Hit);
  not not_19 (not_19_out, S_2);
  not not_20 (not_20_out, Valid);
  not not_21 (not_21_out, Read);
  or or_1 (S_12, and_6_out, and_7_out, and_8_out, and_9_out, and_10_out);
  and and_11 (and_11_out, not_12_out, S_0);
  and and_12 (and_12_out, not_13_out, S_1, Read, not_14_out);
  and and_13 (and_13_out, not_15_out, S_1, Read, not_16_out);
  and and_14 (and_14_out, not_17_out, S_1, Write, not_18_out);
  and and_15 (and_15_out, not_19_out, S_1, Write, not_20_out);
  and and_16 (and_16_out, S_1, S_0, not_21_out);
  or or_2 (S_22, S_0, and_1_out, and_2_out, and_3_out, and_4_out, and_5_out);
  or or_3 (S_02, and_11_out, and_12_out, and_13_out, and_14_out, and_15_out, and_16_out);
endmodule

module CTRL_CacheValidInput (
  input  [2:0] State,
  output ValidInputs
);

  wire not_1_out, not_2_out;

  not not_1 (not_1_out, State[2]);
  not not_2 (not_2_out, State[0]);
  and and_1 (ValidInputs, not_1_out, State[1], not_2_out);
endmodule

module CTRL_CacheReady (
  input  [2:0] State,
  output Ready
);

  wire not_1_out, not_2_out;

  not not_1 (not_1_out, State[2]);
  not not_2 (not_2_out, State[0]);
  and and_1 (Ready, not_1_out, State[1], not_2_out);
endmodule

module CTRL_CacheMemWrite (
  input  [2:0] State,
  output MemWrite
);

  wire not_1_out;

  not not_1 (not_1_out, State[2]);
  and and_1 (MemWrite, not_1_out, State[1], State[0]);
endmodule

module CTRL_CacheMemRead (
  input  [2:0] State,
  output MemRead
);

  and and_1 (MemRead, State[2], State[1], State[0]);
endmodule

module CTRL_BlockByte0Ctrl (
  input  Read,
  input  Write,
  input  O1,
  input  O0,
  output C1,
  output C0
);

  wire not_1_out, not_2_out, not_3_out, not_4_out;

  not not_1 (not_1_out, Read);
  not not_2 (not_2_out, O1);
  not not_3 (not_3_out, O0);
  and and_1 (C0, Read, not_4_out);
  not not_4 (not_4_out, Write);
  and and_2 (C1, not_1_out, Write, not_2_out, not_3_out);
endmodule

module CTRL_BlockByte1Ctrl (
  input  Read,
  input  Write,
  input  O1,
  input  O0,
  output C1,
  output C0
);

  wire not_1_out, not_2_out, not_3_out;

  not not_1 (not_1_out, Read);
  not not_2 (not_2_out, O1);
  and and_1 (C0, Read, not_3_out);
  not not_3 (not_3_out, Write);
  and and_2 (C1, not_1_out, Write, not_2_out, O0);
endmodule

module CTRL_BlockByte2Ctrl (
  input  Read,
  input  Write,
  input  O1,
  input  O0,
  output C1,
  output C0
);

  wire not_1_out, not_2_out, not_3_out;

  not not_1 (not_1_out, Read);
  not not_2 (not_2_out, O0);
  and and_1 (C0, Read, not_3_out);
  not not_3 (not_3_out, Write);
  and and_2 (C1, not_1_out, Write, O1, not_2_out);
endmodule

module CTRL_BlockByte3Ctrl (
  input  Read,
  input  Write,
  input  O1,
  input  O0,
  output C1,
  output C0
);

  wire not_1_out, not_2_out;

  not not_1 (not_1_out, Read);
  and and_1 (C0, Read, not_2_out);
  not not_2 (not_2_out, Write);
  and and_2 (C1, not_1_out, Write, O1, O0);
endmodule

module CTRL_BlockDirtyControl (
  input  Write,
  input  Read,
  output C2,
  output C1
);

  wire not_1_out, not_2_out;

  not not_1 (not_1_out, Read);
  not not_2 (not_2_out, Write);
  and and_1 (C2, Write, not_1_out);
  and and_2 (C1, not_2_out, Read);
endmodule

module CTRL_SetDataOut (
  input  B0Hit,
  input  B1Hit,
  input  B2Hit,
  input  B0Dirty,
  input  B1Dirty,
  input  B2Dirty,
  output C1,
  output C0
);

  wire not_1_out, not_2_out, not_3_out, not_4_out, not_5_out, not_6_out, not_7_out, not_8_out;

  not not_1 (not_1_out, B0Hit);
  not not_2 (not_2_out, B1Hit);
  not not_3 (not_3_out, B0Dirty);
  not not_4 (not_4_out, B1Dirty);
  not not_5 (not_5_out, B0Hit);
  not not_6 (not_6_out, B2Hit);
  not not_7 (not_7_out, B0Dirty);
  not not_8 (not_8_out, B2Dirty);
  and and_1 (C1, not_1_out, not_2_out, not_3_out, not_4_out);
  and and_2 (C0, not_5_out, not_6_out, not_7_out, not_8_out);
endmodule

module CTRL_SetNewAge (
  input  A1,
  input  A0,
  input  N1,
  input  N0,
  output C1,
  output C0
);

  wire and_1_out, and_2_out, and_3_out, and_4_out, and_5_out, and_6_out, and_7_out, and_8_out, and_9_out,
       not_1_out, not_2_out, not_3_out, not_4_out, not_5_out, not_6_out, not_7_out, not_8_out, not_9_out;

  not not_1 (not_1_out, A0);
  and and_1 (and_1_out, not_1_out, N0);
  not not_2 (not_2_out, A1);
  and and_2 (and_2_out, not_2_out, N1);
  and and_3 (and_3_out, A0, not_3_out);
  not not_3 (not_3_out, N0);
  and and_4 (and_4_out, A1, not_4_out);
  not not_4 (not_4_out, N1);
  not not_5 (not_5_out, A1);
  and and_5 (and_5_out, not_5_out, not_6_out);
  not not_6 (not_6_out, A0);
  not not_7 (not_7_out, A1);
  and and_6 (and_6_out, not_7_out, N0);
  not not_8 (not_8_out, A1);
  and and_7 (and_7_out, not_8_out, N1);
  not not_9 (not_9_out, A0);
  and and_8 (and_8_out, not_9_out, N1);
  and and_9 (and_9_out, N1, N0);
  or or_1 (C1, and_1_out, and_2_out, and_3_out, and_4_out);
  or or_2 (C0, and_5_out, and_6_out, and_7_out, and_8_out, and_9_out);
endmodule

module CTRL_SetNewAgeMux (
  input  [2:0] State,
  input  [1:0] Age,
  input  [1:0] AgeAccessed,
  output [1:0] AgeControl
);

  wire [1:0] Control;

  CTRL_SetNewAge ctrl_setnewage_1 (
    .A1(Age[1]), .A0(Age[0]), .N1(AgeAccessed[1]), .N0(AgeAccessed[0]), .C1(Control[1]), .C0(Control[0]));
  Multiplexer #(.select(3), .width(2), .enable("false")) multiplexer_1 (
    .in0(2'b00), .in1(2'b11), .in2(2'b11), .in3(2'b11), .in4(Control), .in5(2'b11), .in6(2'b11), .in7(2'b11),
    .out(AgeControl), .sel(State));
endmodule

module CTRL_CacheDidContain (
  input  S2,
  input  S1,
  input  S12,
  output DidContainControl
);

  wire not_1_out, not_2_out;

  not not_1 (not_1_out, S2);
  not not_2 (not_2_out, S12);
  and and_1 (DidContainControl, not_1_out, S1, not_2_out);
endmodule

module CTRL_SetAgeAcessed (
  input  B0,
  input  B1,
  input  B12,
  output S1,
  output S0
);


  assign S0 = B1;
  assign S1 = B12;
endmodule

module CTRL_CacheStateCacheRead (
  input  [2:0] State,
  output Read
);

  and and_1 (Read, State[0], State[1], State[2]);
endmodule

module CTRL_CacheStateCacheWrite (
  input  [2:0] State,
  output Write
);

  wire and_1_out, and_2_out;

  and and_1 (and_1_out, State[0], State[2]);  // AND_Gate
  or or_1 (Write, and_1_out, and_2_out);
  and and_2 (and_2_out, State[0], State[1]);  // AND_Gate
endmodule

module CTRL_CacheByteRead (
  input  [2:0] State,
  output ByteRead
);

  buf and_1 (ByteRead, State[1]);  // AND_Gate AND_Gate
endmodule

module CTRL_SetLine2Mem (
  input  B0Dirty,
  input  B1Dirty,
  input  B2Dirty,
  output C1,
  output C0
);

  wire and_1_out;

  and and_1 (and_1_out, B0Dirty, B2Dirty);
  or or_1 (C0, B1Dirty, and_1_out);

  assign C1 = B2Dirty;
endmodule
